# Fritzing sketch RobotSchematics (saved by Fritzing 0.9.3b)

parts:
  Part1 = Arduino Mega 2560 (Rev3)
  S1 = H-Bridge with L298N
  GY1 = MPU-6050 Board GY-521 [form="♀ (female)" package=THT]
  M3 = DC Motor
  M2 = DC Motor

nets:
  N1: Part1.D21/SCL, GY1.pin3
  N2: Part1.D20/SDA, GY1.pin4
  5V: Part1.5V, S1.5V, GY1.pin1
  GND: Part1.GND, S1.GND, GY1.pin2
  N3: Part1.D2_PWM, GY1.pin8
  N4: Part1.D3_PWM, S1.ENA
  N5: Part1.D4_PWM, S1.ENB
  N6: Part1.D22, S1.IN1
  N7: Part1.D23, S1.IN4
  N8: Part1.D24, S1.IN2
  N9: Part1.D25, S1.IN3
  N10: S1.M1-01, M2.pin_2
  N11: S1.M1-02, M2.pin_1
  N12: S1.M2-01, M3.pin_2
  N13: S1.M2-02, M3.pin_1

custom parts:
  H-Bridge with L298N: h-bridge
  MPU-6050 Board GY-521: Acelerometro y Giroscopio MPU-6050 Board GY-521
